// Logisim project fsm.circ as structural Verilog: 3 circuits, main circuit main
module main (
  input  in_1,
  output out_2
);

  wire clock_1_out, rom_1_data;
  wire [2:0] register_1_q, \状态转换机_1_n0 ;
  wire [7:0] count;

  Clock #(.highDuration(1), .lowDuration(1)) clock_1 (.out(clock_1_out));
  \状态转换机  \u_状态转换机_1  (
    .S2(register_1_q[2]), .S1(register_1_q[1]), .S0(register_1_q[0]), .cin(rom_1_data), .N2(\状态转换机_1_n0 [2]),
    .N1(\状态转换机_1_n0 [1]), .N0(\状态转换机_1_n0 [0]));
  ROM #(.addrWidth(8), .dataWidth(1), .Select("low")) rom_1 (.addr(count), .data(rom_1_data));
  Counter #(.width(8), .max('hff), .ongoal("wrap"), .trigger("rising"), .behavior("new")) counter_1 (
    .Q(count), .clk(clock_1_out), .clr(in_1));  // open: load, D, count, carry, preset, down
  Register #(.width(3), .trigger("rising"), .Select("low")) register_1 (
    .D(\状态转换机_1_n0 ), .Q(register_1_q), .clk(clock_1_out), .clr(in_1));  // open: en
  \输出函数  \u_输出函数_1  (.S2(register_1_q[2]), .S1(register_1_q[1]), .S0(register_1_q[0]), .cout(out_2));

  // Other names for the same wires on the sheet: reset = in_1

  // Notes on the sheet:
  //   contents of rom_1 (hex, n*v repeats v):
  //   1 0 0 1 0 0 1 0 0 1 0 0 1 0 0 1
endmodule

module \状态转换机  (
  input  S2,
  input  S1,
  input  S0,
  input  cin,
  output N2,
  output N1,
  output N0
);

  wire and_1_out, and_2_out, and_3_out, and_4_out, and_5_out, and_7_out, and_8_out, and_9_out, not_1_out,
       not_2_out, not_3_out, not_4_out, not_5_out, not_6_out, not_7_out, or_2_out;

  and and_1 (and_1_out, S1, S0);
  not not_1 (not_1_out, S1);
  and and_2 (and_2_out, not_1_out, S0);
  not not_2 (not_2_out, cin);
  and and_3 (and_3_out, S1, not_3_out);
  not not_3 (not_3_out, S0);
  not not_4 (not_4_out, cin);
  not not_5 (not_5_out, S1);
  and and_4 (and_4_out, not_5_out, cin);
  and and_5 (and_5_out, S1, not_6_out);
  not not_6 (not_6_out, S0);
  and and_6 (N2, and_1_out, cin);
  and and_7 (and_7_out, and_2_out, not_2_out);
  and and_8 (and_8_out, and_3_out, not_4_out);
  not not_7 (not_7_out, cin);
  or or_1 (N0, and_4_out, and_5_out);
  or or_2 (or_2_out, and_7_out, and_8_out);
  and and_9 (and_9_out, S2, not_7_out);
  or or_3 (N1, or_2_out, and_9_out);
endmodule

module \输出函数  (
  input  S2,
  input  S1,
  input  S0,
  output cout
);


  assign cout = S2;
endmodule
